# Fritzing sketch schema_projet12_FPoiron (saved by Fritzing 0.9.3b)
breadboards: 1

parts:
  Composant1 = Arduino Uno (Rev3)
  LED1 = LED - 5mm [color="Red (633nm)" package="5 mm [THT]"]
  LED2 = LED - 5mm [color="Green (565nm)" package="5 mm [THT]"]
  LED3 = LED - 5mm [color="Yellow (592nm)" package="5 mm [THT]"]
  R1 = Resistor [tolerance=±5% resistance=220 package=THT]
  R2 = Resistor [tolerance=±5% resistance=220 package=THT]
  R3 = Resistor [tolerance=±5% resistance=220 package=THT]
  J1 = Piezo Speaker
  R4 = Resistor [tolerance=±5% resistance=1M package=THT]
  S1 = Pushbutton [package="[THT]"]
  R5 = Resistor [tolerance=±5% resistance=10k package=THT]
  C1 = Electrolytic Capacitor [capacitance=1µF package="100 mil [THT, electrolytic]"]
  J2 = Basic Servo

nets:
  N1: Composant1.A0, J1.pin1, R4.Pin_1
  N2: Composant1.D9_PWM, J2.pulse
  N3: Composant1.D2, S1.Pin_1, S1.Pin_2, R5.Pin_0
  N4: Composant1.D3_PWM, R3.Pin_1
  N5: Composant1.D4, R2.Pin_1
  N6: Composant1.D5_PWM, R1.Pin_1
  5V: Composant1.5V, J1.pin2, S1.Pin_3, S1.Pin_4, C1.-, J2.vcc
  GND: Composant1.GND, LED1.cathode, LED2.cathode, LED3.cathode, R4.Pin_0, R5.Pin_1, C1.+, J2.gnd
  N7: LED1.anode, R1.Pin_0
  N8: LED2.anode, R2.Pin_0
  N9: LED3.anode, R3.Pin_0
